# Fritzing sketch wiring-diagram (saved by Fritzing 0.9.6b)
breadboards: 1

parts:
  Arduino = Arduino Nano (Rev3.0)
  R2 = Resistor [tolerance=±5% power=0.25 resistance=220 package=THT]
  R3 = Resistor [tolerance=±5% power=0.25 resistance=220 package=THT]
  LED_Record = LED - 5mm [color="Red (633nm)" current=0.030 package="5 mm [THT]"]
  LED_Play = LED - 5mm [color="Yellow (595nm)" current=0.030 package="5 mm [THT]"]
  LED_Page = LED - 5mm [color="Yellow (595nm)" current=0.030 package="5 mm [THT]"]
  R1 = Resistor [tolerance=±5% power=0.25 resistance=220 package=THT]
  Btn_Record = SWITCH-MOMENTARY-2 [package=tactile-pth]
  Btn_Play = SWITCH-MOMENTARY-2 [package=tactile-pth]
  Btn_Page = SWITCH-MOMENTARY-2 [package=tactile-pth]
  Btn_Stop = SWITCH-MOMENTARY-2 [package=tactile-pth]
  R4 = Resistor [tolerance=±5% power=0.25 resistance=220 package=THT]
  R5 = Resistor [tolerance=±5% power=0.25 resistance=220 package=THT]
  DIN1 = DIN-5 jack (MIDI) [package=THT]
  J1 = Power Jack [package=power_jack_pth]

nets:
  N1: Arduino.D1/TX, R4.Pin_0
  GND: Arduino.GND, R2.Pin_1, R3.Pin_1, R1.Pin_1, Btn_Record.2, Btn_Play.2, Btn_Page.2, Btn_Stop.2, DIN1.2, J1.GND
  N2: Arduino.D2, Btn_Record.1
  N3: Arduino.D3, Btn_Play.1
  N4: Arduino.D4, Btn_Page.1
  N5: Arduino.D5, Btn_Stop.1
  N6: Arduino.D7, LED_Record.anode
  N7: Arduino.D8, LED_Play.anode
  N8: Arduino.D9, LED_Page.anode
  N9: Arduino.VIN, J1.PWR
  N10: Arduino.5V, R5.Pin_0
  N11: R2.Pin_0, LED_Record.cathode
  N12: R3.Pin_0, LED_Page.cathode
  N13: LED_Play.cathode, R1.Pin_0
  N14: R4.Pin_1, DIN1.5
  N15: R5.Pin_1, DIN1.4
